# Fritzing sketch build-light (saved by Fritzing 0.9.3b)
stripboards: 1

parts:
  Raspberry_Pi_1 = Raspberry Pi 3 [part_number=RPI-3-V1.2]
  LED1 = LED - 5mm [color="Red (633nm)" package="5 mm [THT]"]
  LED2 = LED - 5mm [color="Red (633nm)" package="5 mm [THT]"]
  LED3 = LED - 5mm [color="Red (633nm)" package="5 mm [THT]"]
  R2 = Resistor [tolerance=±5% resistance=330 package=THT]
  R3 = Resistor [tolerance=±5% resistance=330 package=THT]
  R1 = Resistor [tolerance=±5% resistance=330 package=THT]
  S1 = Pushbutton [package="[THT]"]

nets:
  N1: Raspberry_Pi_1.GIPO21, S1.Pin_1, S1.Pin_2
  N2: Raspberry_Pi_1.GND, R2.Pin_1, R3.Pin_1, R1.Pin_1, S1.Pin_3, S1.Pin_4
  N3: LED1.anode, R1.Pin_0
  N4: LED2.anode, R2.Pin_0
  N5: LED3.anode, R3.Pin_0
